// Logisim project cpu.circ as structural Verilog: 1 circuit, main circuit cpu
module cpu (
  input  clk,
  input  [31:0] Instruction,
  input  [31:0] MemReadData,
  output [31:0] MemAddress,
  output [31:0] ProgramCounter,
  output [31:0] ra,
  output [31:0] sp,
  output [31:0] t0,
  output [31:0] t1,
  output [31:0] t2,
  output [31:0] s0,
  output [31:0] s1,
  output [31:0] a0,
  output [3:0] MemWriteMask,
  output [31:0] MemWriteData
);

  wire ASel, BrEq, BrLt, BrUn, BSel, MemWEn, partial_store_1_p5, partial_store_1_p7, partial_store_1_p9,
       PCSel, RegWEn;
  wire [1:0] WBSel;
  wire [2:0] ImmSel;
  wire [3:0] ALUSel;
  wire [31:0] adder_1_out, adder_2_out, DataD, Immediate, multiplexer_1_out, RegReadData1, RegReadData2,
       RegWriteData, ResultA, ResultB;

  Adder #(.width(32)) adder_1 (.a(ProgramCounter), .b(32'h4), .out(adder_1_out));  // open: cin, cout
  Multiplexer #(.enable("false"), .width(32)) multiplexer_1 (
    .in0(adder_1_out), .in1(MemAddress), .out(multiplexer_1_out), .sel(PCSel));
  Register #(.width(32)) PC (.D(multiplexer_1_out), .clk(clk), .Q(ProgramCounter));  // open: en, clr
  control_logic control_logic_1 (
    .PCSel(PCSel), .RegWEn(RegWEn), .ImmSel(ImmSel), .BrUn(BrUn), .ASel(ASel), .BSel(BSel), .ALUSel(ALUSel),
    .MemWEn(MemWEn), .WBSel(WBSel), .Instruction(Instruction), .BrEq(BrEq), .BrLt(BrLt));
  regfile regfile_1 (
    .ReadReg1(Instruction[19:15]), .ReadReg2(Instruction[24:20]), .WriteReg(Instruction[11:7]),
    .RegWriteData(DataD), .RegWEn(RegWEn), .clk(clk), .ra(ra), .sp(sp), .t0(t0), .t1(t1), .t2(t2), .s0(s0),
    .s1(s1), .a0(a0), .RegReadData1(RegReadData1), .RegReadData2(RegReadData2));
  imm_gen imm_gen_1 (.Instruction(Instruction), .ImmSel(ImmSel), .Immediate(Immediate));
  Multiplexer #(.enable("false"), .width(32)) multiplexer_2 (
    .in0(RegReadData2), .in1(Immediate), .out(ResultB), .sel(BSel));
  Multiplexer #(.enable("false"), .width(32)) multiplexer_3 (
    .in0(RegReadData1), .in1(ProgramCounter), .out(ResultA), .sel(ASel));
  // alu alu_1: pin names not known; wires that end beside it: ResultA, ResultB, ALUSel, MemAddress
  Adder #(.width(32)) adder_2 (.a(ProgramCounter), .b(32'h4), .out(adder_2_out));  // open: cin, cout
  Multiplexer #(.enable("false"), .select(2), .width(32)) multiplexer_4 (
    .in0(RegWriteData), .in1(MemAddress), .in2(adder_2_out), .out(DataD), .sel(WBSel));  // open: in3
  // branch_comp branch_comp_1: pin names not known; wires that end beside it: RegReadData1, RegReadData2, BrUn, BrEq, BrLt
  // partial_store partial_store_1: pin names not known; wires that end beside it: Instruction, MemAddress, RegReadData2, MemWEn, partial_store_1_p5, partial_store_1_p5, partial_store_1_p7, partial_store_1_p7, partial_store_1_p9, MemWriteMask, MemWriteData
  partial_load partial_load_1 (
    .Instruction(Instruction), .MemAddress(MemAddress), .DataFromMem(MemReadData), .DataToReg(RegWriteData));

  // Other names for the same wires on the sheet: ALUOut[31:0] = MemAddress; AddrD[4:0] = Instruction[11:7];
  //   AddrA[4:0] = Instruction[19:15]; AddrB[4:0] = Instruction[24:20]

  // Notes on the sheet:
  //   To IMEM
  //   IMEM (do **NOT** move this)
  //   From IMEM
  //   Inputs/Outputs for testing. Do **NOT** move these.
  //   It is OK to move the PC, RegFile, ALU, MEM, Branch Comp, Imm Gen, Partial Load, Partial Store and Control Logic to wherever is most convenient for you when constructing your CPU, and to delete this text
  //   To DMEM
  //   DMEM (do **NOT** move this)
  //   From DMEM
endmodule
